# Fritzing sketch sketch_v1 (saved by Fritzing 0.8.7b)
breadboards: 1

parts:
  WeMos_D1_R1 = WeMos D1 R2
  OLED1 = OLED 128x64 I2C Monochrome Display
  Part1 = Adafruit CCS811
  M1 = BMP280
  Part2 = MQ-7 breakout  # not connected
  S1 = Momentary Switch [package=ksa_sealed_tac_switch]
  S2 = Momentary Switch [package=ksa_sealed_tac_switch]
  S3 = Momentary Switch [package=ksa_sealed_tac_switch]
  R1 = Resistor [tolerance=±5% resistance=10k package=THT]
  R2 = Resistor [tolerance=±5% resistance=150 package=THT]
  R3 = Resistor [tolerance=±5% resistance=47 package=THT]
  SDS1 = SDS011 - dust sensor [part_number=1]  # not connected
  U2 = mystery part, 5 pins [chip_label=?]
  J1 = Screw terminal - 2 pins [package=THT]

nets:
  N1: WeMos_D1_R1.D3, OLED1.SCK, Part1.SCL, M1.SCL
  N2: WeMos_D1_R1.D4, OLED1.SDA, Part1.SDA, M1.SDA
  N3: WeMos_D1_R1.(D5), S3.1, S3.2
  N4: WeMos_D1_R1.(D6), S2.1, S2.2
  N5: WeMos_D1_R1.D11, R1.Pin_0
  N6: WeMos_D1_R1.D12, U2.pin2
  N7: WeMos_D1_R1.D13, U2.pin4
  N8: WeMos_D1_R1.A0, R2.Pin_1, R3.Pin_0
  GND: WeMos_D1_R1.GND, OLED1.GND, Part1.GND, Part1.!WAKE, M1.GND, S1.3, S1.4, S2.3, S2.4, S3.3, S3.4, R3.Pin_1
  3.3V: WeMos_D1_R1.3.3V, OLED1.VDD, Part1.3.3V, M1.VIN
  N9: S1.1, S1.2, R1.Pin_1
  N10: U2.pin3, J1.pin2
  N11: U2.pin5, J1.pin1

notes:
  MQ-2
  10K
  47Ω
  150Ω
  Dust sensor 1.0, 2.5
  DSM501 or PPD42NS
  1 2 3 4 5
  Stable power supply
  5V (with noise reduction)

custom parts:
  WeMos D1 R2: The D1 R2 is a mini wifi board based on the ESP-8266EX.
  BMP280: Temperature Humidity Barometric presure Sensor, I2C
  MQ-7 breakout: SKU: 101282
  SDS011 - dust sensor: The SDS 011 Sensor is a quite recent Air Quality Sensor developed by inovafit, a spin-off from the university of Jinan (in Shandong). With its size, it is probably one of the best sensor in terms of accuracy: While other sensors tend to focus on shrinking the sensor size, the SDS 011 has opted for a size tradeoff allowing it to use a larger fan. And the larger the fan, the better the quality.
